// Logisim project CS240_Rozpedowski_Damian.circ as structural Verilog: 6 circuits, main circuit main
module main (
  input  A3,
  input  A2,
  input  A1,
  input  A0,
  input  B3,
  input  B2,
  input  B1,
  input  B0,
  input  C,
  output out_10,
  output out_11,
  output out_12
);

  _4BitComparatorSignV2 u_4bitcomparatorsignv2_1 (
    .in_9(C), .in_1(A3), .in_2(A2), .in_3(A1), .in_4(A0), .in_5(B3), .in_6(B2), .in_7(B1), .in_8(B0),
    .out_10(out_10), .out_11(out_11), .out_12(out_12));

  // Notes on the sheet:
  //   4 Bit Controlled Comparator
endmodule

module _4BitEqual (
  input  A,
  input  in_2,
  input  in_3,
  input  in_4,
  input  B,
  input  in_6,
  input  in_7,
  input  in_8,
  output out_9
);

  wire not_1_out, not_2_out, not_3_out, not_4_out, xor_1_out, xor_2_out, xor_3_out, xor_4_out;

  xor xor_1 (xor_1_out, A, B);
  not not_1 (not_1_out, xor_1_out);
  xor xor_2 (xor_2_out, in_2, in_6);
  not not_2 (not_2_out, xor_2_out);
  xor xor_3 (xor_3_out, in_3, in_7);
  not not_3 (not_3_out, xor_3_out);
  and and_1 (out_9, not_1_out, not_2_out, not_3_out, not_4_out);
  xor xor_4 (xor_4_out, in_4, in_8);
  not not_4 (not_4_out, xor_4_out);
endmodule

module _4BitGreater (
  input  A,
  input  in_2,
  input  in_3,
  input  in_4,
  input  B,
  input  in_6,
  input  in_7,
  input  in_8,
  output out_9
);

  wire and_1_out, and_2_out, and_3_out, and_4_out, and_5_out, and_6_out, and_7_out, not_1_out, not_2_out,
       not_3_out, not_4_out, not_5_out, not_6_out, not_7_out, not_8_out, not_9_out, not_10_out, xor_1_out,
       xor_2_out, xor_3_out, xor_4_out, xor_5_out, xor_6_out;

  not not_1 (not_1_out, B);
  and and_1 (and_1_out, A, not_1_out);
  xor xor_1 (xor_1_out, A, B);
  not not_2 (not_2_out, xor_1_out);
  not not_3 (not_3_out, in_6);
  and and_2 (and_2_out, in_2, not_3_out);
  and and_3 (and_3_out, not_2_out, and_2_out);
  or or_1 (out_9, and_1_out, and_3_out, and_4_out, and_6_out);
  xor xor_2 (xor_2_out, A, B);
  not not_4 (not_4_out, xor_2_out);
  and and_4 (and_4_out, not_4_out, not_5_out, and_5_out);
  xor xor_3 (xor_3_out, in_2, in_6);
  and and_5 (and_5_out, in_3, not_6_out);
  not not_5 (not_5_out, xor_3_out);
  not not_6 (not_6_out, in_7);
  xor xor_4 (xor_4_out, A, B);
  not not_7 (not_7_out, xor_4_out);
  xor xor_5 (xor_5_out, in_2, in_6);
  not not_8 (not_8_out, xor_5_out);
  xor xor_6 (xor_6_out, in_3, in_7);
  not not_9 (not_9_out, xor_6_out);
  and and_6 (and_6_out, not_7_out, not_8_out, not_9_out, and_7_out);
  not not_10 (not_10_out, in_8);
  and and_7 (and_7_out, in_4, not_10_out);
endmodule

module _4BitLess (
  input  A,
  input  in_2,
  input  in_3,
  input  in_4,
  input  B,
  input  in_6,
  input  in_7,
  input  in_8,
  output out_9
);

  wire and_1_out, and_2_out, and_3_out, and_4_out, and_5_out, and_6_out, and_7_out, not_1_out, not_2_out,
       not_3_out, not_4_out, not_5_out, not_6_out, not_7_out, not_8_out, not_9_out, not_10_out, xor_1_out,
       xor_2_out, xor_3_out, xor_4_out, xor_5_out, xor_6_out;

  not not_1 (not_1_out, A);
  xor xor_1 (xor_1_out, A, B);
  and and_1 (and_1_out, not_1_out, B);
  not not_2 (not_2_out, xor_1_out);
  not not_3 (not_3_out, in_2);
  and and_2 (and_2_out, not_3_out, in_6);
  and and_3 (and_3_out, not_2_out, and_2_out);
  or or_1 (out_9, and_1_out, and_3_out, and_4_out, and_6_out);
  xor xor_2 (xor_2_out, A, B);
  not not_4 (not_4_out, xor_2_out);
  and and_4 (and_4_out, not_4_out, not_6_out, and_5_out);
  not not_5 (not_5_out, in_3);
  xor xor_3 (xor_3_out, in_2, in_6);
  and and_5 (and_5_out, not_5_out, in_7);
  not not_6 (not_6_out, xor_3_out);
  xor xor_4 (xor_4_out, A, B);
  not not_7 (not_7_out, xor_4_out);
  xor xor_5 (xor_5_out, in_2, in_6);
  not not_8 (not_8_out, xor_5_out);
  not not_9 (not_9_out, in_4);
  xor xor_6 (xor_6_out, in_3, in_7);
  not not_10 (not_10_out, xor_6_out);
  and and_6 (and_6_out, not_7_out, not_8_out, not_10_out, and_7_out);
  and and_7 (and_7_out, not_9_out, in_8);
endmodule

module _4BitComparator (
  input  A,
  input  in_2,
  input  in_3,
  input  in_4,
  input  B,
  input  in_6,
  input  in_7,
  input  in_8,
  output out_9,
  output out_10,
  output out_11
);

  _4BitLess u_4bitless_1 (
    .A(A), .in_2(in_2), .in_3(in_3), .in_4(in_4), .B(B), .in_6(in_6), .in_7(in_7), .in_8(in_8), .out_9(out_9));
  _4BitEqual u_4bitequal_1 (
    .A(A), .in_2(in_2), .in_3(in_3), .in_4(in_4), .B(B), .in_6(in_6), .in_7(in_7), .in_8(in_8), .out_9(out_10));
  _4BitGreater u_4bitgreater_1 (
    .A(A), .in_2(in_2), .in_3(in_3), .in_4(in_4), .B(B), .in_6(in_6), .in_7(in_7), .in_8(in_8), .out_9(out_11));
endmodule

module _4BitComparatorSignV2 (
  input  in_1,
  input  in_2,
  input  in_3,
  input  in_4,
  input  in_5,
  input  in_6,
  input  in_7,
  input  in_8,
  input  in_9,
  output out_10,
  output out_11,
  output out_12
);

  wire xor_1_out, xor_2_out;

  xor xor_1 (xor_1_out, in_9, in_1);
  xor xor_2 (xor_2_out, in_9, in_5);
  _4BitComparator u_4bitcomparator_1 (
    .A(xor_1_out), .in_2(in_2), .in_3(in_3), .in_4(in_4), .B(xor_2_out), .in_6(in_6), .in_7(in_7),
    .in_8(in_8), .out_9(out_10), .out_10(out_11), .out_11(out_12));

  // Notes on the sheet:
  //   4 Bit Comp
endmodule
